# Fritzing sketch FingerPrint Reader with servo and leds (saved by Fritzing 0.9.3b)
breadboards: 1

parts:
  Part1 = Arduino Uno (Rev3) - ICSP
  LED1 = LED - 5mm [color="Blue (430nm)" package="5 mm [THT]"]
  LED2 = LED - 5mm [color="Green (555nm)" package="5 mm [THT]"]
  LED3 = LED - 5mm [color="Red (633nm)" package="5 mm [THT]"]
  R1 = Resistor [tolerance=±5% resistance=470 package="2010 [SMD]"]
  R2 = Resistor [tolerance=±5% resistance=470 package="2010 [SMD]"]
  R3 = Resistor [tolerance=±5% resistance=470 package="2010 [SMD]"]
  J1 = Basic Servo
  JP1 = DY50 FINGERPRINT READER [package=1x04-smd]

nets:
  N1: Part1.D8, LED1.anode
  N2: Part1.D12/MISO, J1.pulse
  N3: Part1.D2, JP1.SDA
  N4: Part1.D3_PWM, JP1.SCL
  N5: Part1.D6_PWM, LED3.anode
  N6: Part1.D7, LED2.anode
  VCC: Part1.3V3, J1.vcc, JP1.VCC
  GND: Part1.GND, R1.Pin_1, R2.Pin_1, R3.Pin_1, J1.gnd, JP1.GND
  N7: LED1.cathode, R2.Pin_0
  N8: LED2.cathode, R3.Pin_0
  N9: LED3.cathode, R1.Pin_0

custom parts:
  DY50 FINGERPRINT READER: FINGERPRINT READER SENSOR MODEL DY50 3,3V
